# Fritzing sketch ESP32_MPU6050 (saved by Fritzing 0.9.3b)

parts:
  SparkFun_ESP32_Thing1 = SparkFun ESP32 Thing [part_number=DEV-13907]
  GY1 = MPU-6050 Board GY-521 [form="♀ (female)" package=THT]

nets:
  N1: SparkFun_ESP32_Thing1.GND, GY1.pin2
  N2: SparkFun_ESP32_Thing1.3.3V, GY1.pin1
  N3: SparkFun_ESP32_Thing1.22, GY1.pin3
  N4: SparkFun_ESP32_Thing1.21, GY1.pin4

custom parts:
  SparkFun ESP32 Thing: The SparkFun ESP32 Thing is a comprehensive development platform for Espressif’s ESP32, their super-charged version of the popular ESP8266. Like the 8266, the ESP32 is a WiFi-compatible microcontroller, but to that it adds support for Bluetooth low-energy (i.e BLE, BT4.0, Bluetooth Smart), and nearly 30 I/O pins. The ESP32’s power and versatility will make it the foundation of IoT and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
  MPU-6050 Board GY-521: Acelerometro y Giroscopio MPU-6050 Board GY-521
